# Fritzing sketch Bibliobot (saved by Fritzing 0.9.9b)
breadboards: 1

parts:
  MCU1 = Raspberry Pi Zero
  HC-SR04_Sensor_1 = HC-SR04 Ultrasonic Distance Sensor
  HC-SR04_Sensor_2 = HC-SR04 Ultrasonic Distance Sensor
  HC-SR04_Sensor_3 = HC-SR04 Ultrasonic Distance Sensor
  SP1 = SPEAKER [package=pcb_mount_speaker]
  U2 = LIPO-1000mAh [package=lipo-1000]
  Componente1 = Motor Driver 1A Dual TB6612FNG
  DFRobot_DFPlayer_Mini1 = DFRobot DFPlayer Mini [part_number=DFR0299]
  M1 = DC Motor
  R1 = Resistor [tolerance=±5% resistance=220 package="2010 [SMD]"]
  R2 = Resistor [tolerance=±5% resistance=220 package="2010 [SMD]"]
  R3 = Resistor [tolerance=±5% resistance=220 package="2010 [SMD]"]
  R4 = Resistor [tolerance=±5% resistance=220 package="2010 [SMD]"]
  R5 = Resistor [tolerance=±5% resistance=220 package="2010 [SMD]"]
  R6 = Resistor [tolerance=±5% resistance=220 package="2010 [SMD]"]
  M2 = DC Motor
  Componente7 = Compass Module - HMC6352
  Componente9 = Adafruit Stereo 2.8W Class D Audio Amplifier - I2C Control AGC - TPA2016 [part_number="Adafruit #1712"]
  Componente10 = Adafruit I2S Mic - SPH0645 [part_number="Adafruit #3421"]
  Componente11 = Adafruit I2S Mic - SPH0645 [part_number="Adafruit #3421"]
  Componente12 = Adafruit I2S Mic - SPH0645 [part_number="Adafruit #3421"]

nets:
  VCC: MCU1.pin_2, MCU1.pin_3, MCU1.pin_4, HC-SR04_Sensor_1.VCC, HC-SR04_Sensor_2.VCC, HC-SR04_Sensor_3.VCC, Componente1.VCC, DFRobot_DFPlayer_Mini1.VCC, Componente7.VCC, Componente7.SDA, Componente10.VDD, Componente11.VDD, Componente12.VDD
  N1: MCU1.pin_5, Componente7.SCL
  GND: MCU1.pin_6, MCU1.pin_9, MCU1.pin_14, MCU1.pin_19, MCU1.pin_20, MCU1.pin_25, MCU1.pin_29, MCU1.pin_30, HC-SR04_Sensor_1.GND, HC-SR04_Sensor_2.GND, HC-SR04_Sensor_3.GND, U2.-, Componente1.GND, R2.Pin_0, R4.Pin_0, R6.Pin_0, Componente7.GND, Componente10.GND, Componente10.BCLK, Componente10.DATA, Componente11.GND, Componente12.GND, Componente12.DATA
  N2: MCU1.pin_8, DFRobot_DFPlayer_Mini1.RX
  N3: MCU1.pin_12, HC-SR04_Sensor_3.TRIG
  N4: MCU1.pin_16, HC-SR04_Sensor_2.TRIG
  N5: MCU1.pin_18, R1.Pin_1, R2.Pin_1
  N6: MCU1.pin_21, Componente11.DATA
  N7: MCU1.pin_22, R3.Pin_1, R4.Pin_1
  N8: MCU1.pin_23, Componente12.BCLK
  N9: MCU1.pin_27, Componente10.WS
  N10: MCU1.pin_31, Componente11.WS
  N11: MCU1.pin_32, HC-SR04_Sensor_1.TRIG
  N12: MCU1.pin_35, Componente12.WS, Componente12.SELECT
  N13: MCU1.pin_36, R5.Pin_1, R6.Pin_1
  N14: MCU1.pin_40, Componente11.BCLK
  N15: HC-SR04_Sensor_1.ECHO, R5.Pin_0
  N16: HC-SR04_Sensor_2.ECHO, R3.Pin_0
  N17: HC-SR04_Sensor_3.ECHO, R1.Pin_0
  N18: SP1.+, Componente9.OUT_R_N
  N19: SP1.-, Componente9.OUT_R_P
  N20: U2.+, Componente1.VM
  N21: Componente1.B01, M1.pin_1
  N22: Componente1.B02, M1.pin_2
  N23: Componente1.A02, M2.pin_1
  N24: Componente1.A01, M2.pin_2
  N25: DFRobot_DFPlayer_Mini1.DAC_R, Componente9.IN_R_P
  N26: DFRobot_DFPlayer_Mini1.GND-1, DFRobot_DFPlayer_Mini1.GND-2, Componente9.IN_R_N

custom parts:
  Adafruit Stereo 2.8W Class D Audio Amplifier - I2C Control AGC - TPA2016: A mini class D with AGC and I2C control? Yes please! This incredibly small stereo amplifier is surprisingly powerful. It is able to deliver 2 x 2.8W channels into 4 ohm impedance speakers (@ 10% THD) and it has a i2c control interface as well as an AGC (automatic gain control) system to keep your audio from clipping or distorting. If you don't want to use I2C to control it, it does start up on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
  Adafruit I2S Mic - SPH0645: For many microcontrollers, adding audio input is easy with one of our analog microphone breakouts. But as you get to bigger and better microcontrollers and microcomputers, you'll find that you don't always have an analog input, or maybe you want to avoid the noise that can seep in with an analog mic system. Once you get past 8-bit micros, you will often find an I2S peripheral, that can take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
